// Logisim project pgm1.circ as structural Verilog: 2 circuits, main circuit main
module main (
  input  X,
  input  Y,
  input  X_2,
  input  Y_2,
  input  X_3,
  input  X_4,
  input  Y_3,
  input  X_5,
  input  Y_4,
  output X_Y,
  output X_Y_2,
  output nX,
  output X_Y_3,
  output X_Y_4
);

  or or_1 (X_Y, X, Y);
  and and_1 (X_Y_2, X_2, Y_2);
  not not_1 (nX, X_3);
  xor xor_1 (X_Y_3, X_4, Y_3);
  xnor xnor_1 (X_Y_4, X_5, Y_4);
endmodule

module f_a_b_c (
  input  a,
  input  b,
  input  c,
  output f
);

  wire and_1_out, not_1_out;

  not not_1 (not_1_out, a);
  and and_1 (and_1_out, not_1_out, b);
  or or_1 (f, c, and_1_out);
endmodule
