// Logisim project pgm11.circ as structural Verilog: 3 circuits, main circuit main
module main (
  input  x,
  input  y,
  input  x_2,
  input  y_2,
  input  x_3,
  output out_6,
  output out_7,
  output nx
);

  wire nor_1_out, nor_2_out, nor_3_out;

  nor nor_1 (nor_1_out, x, y);
  nor nor_2 (nor_2_out, x_2, x_2);
  nor nor_3 (nor_3_out, y_2, y_2);
  nor nor_4 (nx, x_3, x_3);
  nor nor_5 (out_7, nor_2_out, nor_3_out);
  nor nor_6 (out_6, nor_1_out, nor_1_out);

  // Notes on the sheet:
  //   (x+y)
  //   'x,'y
  //   'x.'y
  //   'x
  //   'y
  //   x+y
  //   x.y
endmodule

module f_a_b_c (
  input  a,
  input  b,
  input  c,
  output f
);

  wire and_1_out, and_2_out, and_3_out, and_4_out, not_1_out, not_2_out, not_3_out, or_1_out;

  not not_1 (not_1_out, a);
  not not_2 (not_2_out, b);
  and and_1 (and_1_out, not_1_out, not_2_out);
  not not_3 (not_3_out, c);
  and and_2 (and_2_out, and_1_out, c);
  and and_3 (and_3_out, b, not_3_out);
  or or_1 (or_1_out, and_2_out, and_3_out);
  and and_4 (and_4_out, a, b);
  or or_2 (f, or_1_out, and_4_out);
endmodule

module f_a_b_c_2 (
  input  a,
  input  b,
  input  c,
  output f
);

  wire and_1_out, and_2_out, and_3_out, and_4_out, not_1_out, not_2_out, not_3_out, or_1_out;

  not not_1 (not_1_out, a);
  not not_2 (not_2_out, b);
  and and_1 (and_1_out, not_1_out, not_2_out);
  not not_3 (not_3_out, c);
  and and_2 (and_2_out, and_1_out, c);
  and and_3 (and_3_out, b, not_3_out);
  or or_1 (or_1_out, and_2_out, and_3_out);
  and and_4 (and_4_out, a, b);
  or or_2 (f, or_1_out, and_4_out);
endmodule
