// Logisim project pgm15.circ as structural Verilog: 1 circuit, main circuit main
module main (
  input  in_1,
  input  in_2,
  input  in_3,
  input  in_4,
  output out_5,
  output out_6,
  output out_7,
  output out_8,
  output out_9,
  output out_10
);

  wire clock_1_out, clock_2_out, clock_3_out;

  Clock clock_1 (.out(clock_1_out));
  Clock clock_2 (.out(clock_2_out));
  Clock clock_3 (.out(clock_3_out));
  D_Flip_Flop d_ff_1 (.clk(clock_2_out), .D(in_3), .Q(out_7));  // open: Qn, preset, en, reset
  T_Flip_Flop t_ff_1 (.clk(clock_3_out), .T(in_4), .Q(out_9));  // open: Qn, preset, reset, en
  J_K_Flip_Flop j_k_ff_1 (.J(in_1), .clk(clock_1_out), .K(in_2), .Q(out_5));  // open: Qn, preset, en, reset

  assign out_6 = out_5;
  assign out_8 = out_7;
  assign out_10 = out_9;
endmodule
