// Logisim project pgm16.circ as structural Verilog: 1 circuit, main circuit main
module main (
  input  in_1,
  input  in_2,
  input  in_3,
  input  in_4,
  input  in_5,
  input  in_6,
  input  in_7,
  output out_8,
  output out_9
);

  wire and_1_out, and_2_out, and_3_out, and_4_out, and_5_out, and_6_out, button_1_out, button_2_out,
       button_3_out, button_4_out, clock_1_out, clock_2_out, clock_3_out, clock_4_out, d_ff_1_q, d_ff_2_q,
       d_ff_3_q, d_ff_4_q, d_ff_5_q, d_ff_6_q, d_ff_7_q, d_ff_8_q, d_ff_11_q, d_ff_12_q, d_ff_13_q,
       d_ff_16_q, not_1_out, or_1_out, undriven;

  Clock clock_1 (.out(clock_1_out));
  Button button_1 (.out(button_1_out));
  Clock clock_2 (.out(clock_2_out));
  Button button_2 (.out(button_2_out));
  Clock clock_3 (.out(clock_3_out));
  Button button_3 (.out(button_3_out));
  LED led_1 (.in(d_ff_1_q));
  D_Flip_Flop d_ff_1 (.clk(clock_1_out), .D(in_3), .Q(d_ff_1_q), .en(button_1_out));  // open: Qn, preset, reset
  D_Flip_Flop d_ff_2 (.clk(clock_2_out), .D(clock_2_out), .Q(d_ff_2_q), .en(button_2_out));  // open: Qn, preset, reset
  LED led_2 ();  // open: in
  D_Flip_Flop d_ff_3 (.clk(clock_3_out), .D(in_1), .Q(d_ff_3_q), .en(button_3_out));  // open: Qn, preset, reset
  D_Flip_Flop d_ff_4 (.clk(clock_1_out), .D(d_ff_1_q), .Q(d_ff_4_q), .en(button_1_out));  // open: Qn, preset, reset
  D_Flip_Flop d_ff_5 (.clk(clock_2_out), .D(clock_2_out), .Q(d_ff_5_q), .en(button_2_out));  // open: Qn, preset, reset
  LED led_3 ();  // open: in
  LED led_4 (.in(d_ff_4_q));
  LED led_5 (.in(d_ff_6_q));
  D_Flip_Flop d_ff_6 (.clk(clock_1_out), .D(d_ff_4_q), .Q(d_ff_6_q), .en(button_1_out));  // open: Qn, preset, reset
  D_Flip_Flop d_ff_7 (.clk(clock_2_out), .D(clock_2_out), .Q(d_ff_7_q), .en(button_2_out));  // open: Qn, preset, reset
  LED led_6 ();  // open: in
  D_Flip_Flop d_ff_8 (.clk(clock_3_out), .D(d_ff_3_q), .Q(d_ff_8_q), .en(button_3_out));  // open: Qn, preset, reset
  D_Flip_Flop d_ff_9 (.clk(clock_1_out), .D(d_ff_6_q), .Q(out_8), .en(button_1_out));  // open: Qn, preset, reset
  LED led_7 (.in(out_8));
  D_Flip_Flop d_ff_10 (.clk(clock_2_out), .D(clock_2_out), .Q(out_9), .en(button_2_out));  // open: Qn, preset, reset
  LED led_8 ();  // open: in
  D_Flip_Flop d_ff_11 (.clk(clock_3_out), .D(d_ff_8_q), .Q(d_ff_11_q), .en(button_3_out));  // open: Qn, preset, reset
  Clock clock_4 (.out(clock_4_out));
  Button button_4 (.out(button_4_out));
  D_Flip_Flop d_ff_12 (.clk(clock_3_out), .D(d_ff_11_q), .Q(d_ff_12_q), .en(button_3_out));  // open: Qn, preset, reset
  // NOT_Gate not_1 has open pins: in=open, out=not_1_out
  D_Flip_Flop d_ff_13 (.Q(d_ff_13_q));  // open: clk, D, Qn, preset, en, reset
  LED led_9 (.in(d_ff_12_q));
  buf and_1 (and_1_out, d_ff_13_q);  // AND_Gate
  // AND_Gate and_2 has open pins: out=and_2_out
  or or_1 (or_1_out, and_1_out, and_2_out);
  // AND_Gate and_3 has open pins: out=and_3_out
  D_Flip_Flop d_ff_14 (.D(or_1_out));  // open: clk, Q, Qn, preset, en, reset
  // AND_Gate and_4 has open pins: out=and_4_out
  // OR_Gate or_2 has open pins: in0=and_3_out, in4=and_4_out, out=open
  D_Flip_Flop d_ff_15 ();  // open: clk, D, Q, Qn, preset, en, reset
  // AND_Gate and_5 has open pins: out=and_5_out
  // OR_Gate or_3 has open pins: in0=and_5_out, in4=and_6_out, out=open
  and and_6 (and_6_out, not_1_out, undriven);
  LED led_10 (.in(d_ff_16_q));
  D_Flip_Flop d_ff_16 (.clk(clock_4_out), .Q(d_ff_16_q), .en(button_4_out));  // open: D, Qn, preset, reset
endmodule
