// Logisim project pgm8.circ as structural Verilog: 1 circuit, main circuit main
module main (
  input  A,
  input  B,
  input  C_IN,
  output sum
);

  wire and_1_out, and_2_out, or_1_out, xor_1_out;

  xor xor_1 (xor_1_out, A, B);
  and and_1 (and_1_out, B, A);
  xor xor_2 (sum, xor_1_out, C_IN);
  and and_2 (and_2_out, xor_1_out, C_IN);
  or or_1 (or_1_out, and_2_out, and_1_out);
endmodule
